# Fritzing sketch sketch (saved by Fritzing 0.9.3b)
circuit board: 10cm x 7cm
breadboards: 2

parts:
  Part1 = Motor Driver 1A Dual TB6612FNG
  U1 = NodeMCU V1.0
  Omega = female pin header, 2 pins [form="♀ (female)"]
  Rolex = female pin header, 2 pins [form="♀ (female)"]
  PWR = female pin header, 2 pins [form="♀ (female)"]
  On = female pin header, 2 pins [form="♀ (female)"]
  74HC4051 = 74HC595 [package="DIP16 [THT]"]
  J1 = female pin header, 2 pins [form="♀ (female)"]
  J2 = female pin header, 2 pins [form="♀ (female)"]
  J3 = female pin header, 2 pins [form="♀ (female)"]
  J4 = female pin header, 2 pins [form="♀ (female)"]

nets:
  GND: Part1.GND, U1.GND, PWR.pin2, 74HC4051.Q6, 74HC4051.Q7, 74HC4051.GND
  N1: Part1.B01, Omega.pin1
  N2: Part1.B02, Omega.pin2
  N3: Part1.A02, Rolex.pin1
  N4: Part1.A01, Rolex.pin2
  VCC: Part1.VCC, U1.3V3
  VIN: Part1.VM, U1.Vin, On.pin2, 74HC4051.VCC, J2.pin2, J3.pin2
  N5: Part1.PWMA, U1.D8
  N6: Part1.AIN2, U1.D7
  N7: Part1.AIN1, U1.D6
  N8: Part1.STBY, U1.D5
  N9: Part1.BIN1, U1.D4
  N10: Part1.BIN2, U1.D2
  N11: Part1.PWMB, U1.D1
  N12: U1.RX, 74HC4051.SH_CP
  N13: U1.TX, 74HC4051.MR
  N14: U1.SD2, 74HC4051.Q3
  N15: U1.SD3, 74HC4051.Q7'
  N16: PWR.pin1, On.pin1
  N17: 74HC4051.Q1, J4.pin2
  N18: 74HC4051.Q5, J4.pin1
  N19: 74HC4051.ST_CP, J3.pin1
  N20: 74HC4051.OE, J2.pin1
  N21: 74HC4051.DS, J1.pin2
  N22: 74HC4051.Q0, J1.pin1

custom parts:
  NodeMCU V1.0: ESP8266 based NodeMCU
